// Logisim project my_ALU.circ as structural Verilog: 15 circuits, main circuit main
module main (
  input  [7:0] in_1,
  input  [2:0] in_2,
  output [7:0] out_3
);

  Shifter shifter_1 (.in(in_1), .\dist (in_2), .out(out_3));
endmodule

module Adder_1 (
  input  Carry_in,
  input  Input_A,
  input  Input_B,
  output Carry_out,
  output Output_A_B
);

  wire and_1_out, and_2_out, and_3_out, and_4_out, and_5_out, and_6_out, and_7_out, and_8_out, not_1_out,
       not_2_out, not_3_out, not_4_out, not_5_out, not_6_out, not_7_out, not_8_out, not_9_out;

  not not_1 (not_1_out, Carry_in);
  not not_2 (not_2_out, Input_A);
  not not_3 (not_3_out, Input_B);
  not not_4 (not_4_out, Carry_in);
  not not_5 (not_5_out, Input_A);
  not not_6 (not_6_out, Carry_in);
  not not_7 (not_7_out, Input_B);
  not not_8 (not_8_out, Input_A);
  not not_9 (not_9_out, Input_B);
  and and_1 (and_1_out, not_1_out, Input_A, Input_B);
  and and_2 (and_2_out, Carry_in, not_2_out, Input_B);
  and and_3 (and_3_out, Carry_in, Input_A, not_3_out);
  and and_4 (and_4_out, Carry_in, Input_A, Input_B);
  and and_5 (and_5_out, not_4_out, not_5_out, Input_B);
  and and_6 (and_6_out, not_6_out, Input_A, not_7_out);
  and and_7 (and_7_out, Carry_in, not_8_out, not_9_out);
  and and_8 (and_8_out, Carry_in, Input_A, Input_B);
  or or_1 (Carry_out, and_1_out, and_2_out, and_3_out, and_4_out);
  or or_2 (Output_A_B, and_5_out, and_6_out, and_7_out, and_8_out);
endmodule

module Adder_2 (
  input  [1:0] Input_A_2,
  input  [1:0] Input_B_2,
  output out_3,
  output out_4,
  output out_5
);

  wire adder_1_cout;

  Adder #(.width(1)) adder_1 (.a(Input_A_2[0]), .b(Input_B_2[0]), .out(out_3), .cin(1'b0), .cout(adder_1_cout));
  Adder #(.width(1)) adder_2 (.a(Input_A_2[1]), .b(Input_B_2[1]), .out(out_4), .cin(adder_1_cout), .cout(out_5));
endmodule

module SubTractor_1 (
  input  Borrow_in,
  input  Input_A,
  input  Input_B,
  output Borrow_out,
  output Output_A_B
);

  wire and_1_out, and_2_out, and_3_out, and_4_out, and_5_out, and_6_out, and_7_out, not_1_out, not_2_out,
       not_3_out;

  not not_1 (not_1_out, Borrow_in);
  not not_2 (not_2_out, Input_A);
  not not_3 (not_3_out, Input_B);
  and and_1 (and_1_out, not_2_out, Input_B);
  and and_2 (and_2_out, Borrow_in, not_2_out);
  and and_3 (and_3_out, Borrow_in, Input_B);
  and and_4 (and_4_out, not_1_out, not_2_out, Input_B);
  and and_5 (and_5_out, not_1_out, Input_A, not_3_out);
  and and_6 (and_6_out, Borrow_in, not_2_out, not_3_out);
  and and_7 (and_7_out, Borrow_in, Input_A, Input_B);
  or or_1 (Borrow_out, and_1_out, and_2_out, and_3_out);
  or or_2 (Output_A_B, and_4_out, and_5_out, and_6_out, and_7_out);
endmodule

module Negator_8 (
  input  [7:0] in_1,
  output [7:0] out_2
);

  wire [7:0] not_1_out;

  assign not_1_out = ~in_1;  // NOT_Gate not_1, 8 bits wide
  Adder adder_1 (.a(not_1_out), .b(8'h1), .out(out_2), .cin(1'b0));  // open: cout
endmodule

module Comparator_1_unsigned (
  input  Input_A,
  input  Input_B,
  output gt,
  output eq,
  output lt
);

  wire and_2_out, and_3_out, not_1_out, not_2_out;

  not not_1 (not_1_out, Input_A);
  not not_2 (not_2_out, Input_B);
  and and_1 (gt, Input_A, not_2_out);
  and and_2 (and_2_out, not_1_out, not_2_out);
  and and_3 (and_3_out, Input_A, Input_B);
  and and_4 (lt, not_1_out, Input_B);
  or or_1 (eq, and_2_out, and_3_out);
endmodule

module Comparator_2_unsigned (
  input  [1:0] Input_A_2,
  input  [1:0] Input_B_2,
  output gt,
  output eq,
  output lt
);

  wire comparator_1_unsigned_1_eq, comparator_1_unsigned_1_gt, comparator_1_unsigned_1_lt,
       comparator_1_unsigned_2_eq, comparator_1_unsigned_2_gt, comparator_1_unsigned_2_lt, not_1_out,
       not_2_out;

  Comparator_1_unsigned comparator_1_unsigned_1 (
    .Input_A(Input_A_2[1]), .Input_B(Input_B_2[1]), .gt(comparator_1_unsigned_1_gt),
    .eq(comparator_1_unsigned_1_eq), .lt(comparator_1_unsigned_1_lt));
  Comparator_1_unsigned comparator_1_unsigned_2 (
    .Input_A(Input_A_2[0]), .Input_B(Input_B_2[0]), .gt(comparator_1_unsigned_2_gt),
    .eq(comparator_1_unsigned_2_eq), .lt(comparator_1_unsigned_2_lt));
  not not_1 (not_1_out, comparator_1_unsigned_1_eq);
  not not_2 (not_2_out, comparator_1_unsigned_1_eq);
  assign gt = not_1_out ? comparator_1_unsigned_1_gt : 1'bz;  // Controlled_Buffer controlled_buffer_1
  assign lt = not_2_out ? comparator_1_unsigned_1_lt : 1'bz;  // Controlled_Buffer controlled_buffer_2
  assign gt = comparator_1_unsigned_1_eq ? comparator_1_unsigned_2_gt : 1'bz;  // Controlled_Buffer controlled_buffer_3
  assign eq = comparator_1_unsigned_1_eq ? comparator_1_unsigned_2_eq : 1'bz;  // Controlled_Buffer controlled_buffer_4
  assign lt = comparator_1_unsigned_1_eq ? comparator_1_unsigned_2_lt : 1'bz;  // Controlled_Buffer controlled_buffer_5
endmodule

module Comparator_2_unsigned_violent (
  input  [1:0] A,
  input  [1:0] B,
  output gt,
  output eq,
  output lt
);

  wire and_1_out, and_2_out, and_3_out, and_4_out, and_5_out, and_6_out, and_7_out, and_8_out, and_9_out,
       and_10_out, not_1_out, not_2_out, not_3_out, not_4_out;

  not not_1 (not_1_out, A[1]);
  not not_2 (not_2_out, A[0]);
  not not_3 (not_3_out, B[1]);
  not not_4 (not_4_out, B[0]);
  and and_1 (and_1_out, A[0], not_3_out, not_4_out);
  and and_2 (and_2_out, A[1], not_3_out);
  and and_3 (and_3_out, A[1], A[0], not_4_out);
  and and_4 (and_4_out, not_1_out, not_2_out, not_3_out, not_4_out);
  and and_5 (and_5_out, not_1_out, A[0], not_3_out, B[0]);
  and and_6 (and_6_out, A[1], not_2_out, B[1], not_4_out);
  and and_7 (and_7_out, A[1], A[0], B[1], B[0]);
  and and_8 (and_8_out, not_1_out, not_2_out, B[0]);
  and and_9 (and_9_out, not_1_out, B[1]);
  and and_10 (and_10_out, not_2_out, B[1], B[0]);
  or or_1 (gt, and_1_out, and_2_out, and_3_out);
  or or_2 (eq, and_4_out, and_5_out, and_6_out, and_7_out);
  or or_3 (lt, and_8_out, and_9_out, and_10_out);
endmodule

module Comparator_8_complement (
  input  [7:0] A,
  input  [7:0] B,
  output gt,
  output eq,
  output lt
);

  wire auxiliary_comparator_8_complement_1_eq, auxiliary_comparator_8_complement_1_gt,
       auxiliary_comparator_8_complement_1_lt, comparator_1_eq, comparator_1_gt, comparator_1_lt,
       comparator_2_eq, comparator_2_gt, comparator_2_lt, flag_eq_height_and_eq_out, not_1_out, not_2_out,
       not_3_out, or_1_out;

  Comparator #(.mode("unsigned"), .width(1)) comparator_1 (
    .a(A[7]), .b(B[7]), .gt(comparator_1_gt), .eq(comparator_1_eq), .lt(comparator_1_lt));
  and flag_eq_height_and_eq (flag_eq_height_and_eq_out, comparator_1_eq, B[7]);
  Comparator #(.mode("unsigned"), .width(7)) comparator_2 (
    .a(A[6:0]), .b(B[6:0]), .gt(comparator_2_gt), .eq(comparator_2_eq), .lt(comparator_2_lt));
  not not_1 (not_1_out, comparator_1_eq);
  assign lt = not_1_out ? comparator_1_gt : 1'bz;  // Controlled_Buffer controlled_buffer_1
  assign gt = not_2_out ? comparator_1_lt : 1'bz;  // Controlled_Buffer controlled_buffer_2
  not not_2 (not_2_out, comparator_1_eq);
  or or_1 (or_1_out, comparator_1_lt, comparator_1_gt);
  not not_3 (not_3_out, or_1_out);
  auxiliary_comparator_8_complement auxiliary_comparator_8_complement_1 (
    .flag(flag_eq_height_and_eq_out), .gt_in(comparator_2_gt), .eq_in(comparator_2_eq),
    .lt_in(comparator_2_lt), .gt(auxiliary_comparator_8_complement_1_gt),
    .eq(auxiliary_comparator_8_complement_1_eq), .lt(auxiliary_comparator_8_complement_1_lt));
  assign gt = not_3_out ? auxiliary_comparator_8_complement_1_gt : 1'bz;  // Controlled_Buffer controlled_buffer_3
  assign eq = not_3_out ? auxiliary_comparator_8_complement_1_eq : 1'bz;  // Controlled_Buffer controlled_buffer_4
  assign lt = not_3_out ? auxiliary_comparator_8_complement_1_lt : 1'bz;  // Controlled_Buffer controlled_buffer_5
endmodule

module auxiliary_comparator_8_complement (
  input  flag,
  input  gt_in,
  input  eq_in,
  input  lt_in,
  output gt,
  output eq,
  output lt
);

  wire and_1_out, and_2_out, and_3_out, and_4_out, not_1_out;

  not not_1 (not_1_out, flag);
  and and_1 (and_1_out, not_1_out, gt_in);
  and and_2 (and_2_out, flag, lt_in);
  and and_3 (and_3_out, not_1_out, lt_in);
  and and_4 (and_4_out, flag, gt_in);
  or or_1 (gt, and_1_out, and_2_out);
  or or_2 (lt, and_3_out, and_4_out);

  assign eq = eq_in;
endmodule

module Shift_Right_Logic_8bit (
  input  [7:0] Data_input,
  output [7:0] Output_srl_7,
  output [7:0] Output_srl_6,
  output [7:0] Output_srl_5,
  output [7:0] Output_srl_4,
  output [7:0] Output_srl_3,
  output [7:0] Output_srl_2,
  output [7:0] Output_srl_1,
  output [7:0] Output_srl_0
);


  assign Output_srl_0 = Data_input;
  assign Output_srl_1 = {1'b0, Data_input[7:1]};
  assign Output_srl_2 = {2'b00, Data_input[7:2]};
  assign Output_srl_3 = {3'b000, Data_input[7:3]};
  assign Output_srl_4 = {4'b0000, Data_input[7:4]};
  assign Output_srl_5 = {{5{1'b0}}, Data_input[7:5]};
  assign Output_srl_6 = {{6{1'b0}}, Data_input[7:6]};
  assign Output_srl_7 = {{7{1'b0}}, Data_input[7]};
endmodule

module Shift_Right_Logic_8bit_complete (
  input  [7:0] in_1,
  input  [2:0] in_2,
  output [7:0] out_3
);

  wire [7:0] shift_right_logic_8bit_1_output_srl_0, shift_right_logic_8bit_1_output_srl_1,
       shift_right_logic_8bit_1_output_srl_2, shift_right_logic_8bit_1_output_srl_3,
       shift_right_logic_8bit_1_output_srl_4, shift_right_logic_8bit_1_output_srl_5,
       shift_right_logic_8bit_1_output_srl_6, shift_right_logic_8bit_1_output_srl_7;

  Shift_Right_Logic_8bit shift_right_logic_8bit_1 (
    .Data_input(in_1), .Output_srl_7(shift_right_logic_8bit_1_output_srl_7),
    .Output_srl_6(shift_right_logic_8bit_1_output_srl_6),
    .Output_srl_5(shift_right_logic_8bit_1_output_srl_5),
    .Output_srl_4(shift_right_logic_8bit_1_output_srl_4),
    .Output_srl_3(shift_right_logic_8bit_1_output_srl_3),
    .Output_srl_2(shift_right_logic_8bit_1_output_srl_2),
    .Output_srl_1(shift_right_logic_8bit_1_output_srl_1), .Output_srl_0(shift_right_logic_8bit_1_output_srl_0));
  Multiplexer #(.select(3), .width(8)) multiplexer_1 (
    .in0(shift_right_logic_8bit_1_output_srl_0), .in1(shift_right_logic_8bit_1_output_srl_1),
    .in2(shift_right_logic_8bit_1_output_srl_2), .in3(shift_right_logic_8bit_1_output_srl_3),
    .in4(shift_right_logic_8bit_1_output_srl_4), .in5(shift_right_logic_8bit_1_output_srl_5),
    .in6(shift_right_logic_8bit_1_output_srl_6), .in7(shift_right_logic_8bit_1_output_srl_7), .out(out_3),
    .sel(in_2));
endmodule

module Shift_Right_Algorithm_8bit (
  input  [7:0] Data_input,
  output [7:0] Output_sra_7,
  output [7:0] Output_sra_6,
  output [7:0] Output_sra_5,
  output [7:0] Output_sra_4,
  output [7:0] Output_sra_3,
  output [7:0] Output_sra_2,
  output [7:0] Output_sra_1,
  output [7:0] Output_sra_0
);


  assign Output_sra_0 = Data_input;
  assign Output_sra_1 = {{2{Data_input[7]}}, Data_input[6:1]};
  assign Output_sra_2 = {{3{Data_input[7]}}, Data_input[6:2]};
  assign Output_sra_3 = {{4{Data_input[7]}}, Data_input[6:3]};
  assign Output_sra_4 = {{5{Data_input[7]}}, Data_input[6:4]};
  assign Output_sra_5 = {{6{Data_input[7]}}, Data_input[6:5]};
  assign Output_sra_6 = {{7{Data_input[7]}}, Data_input[6]};
  assign Output_sra_7 = {8{Data_input[7]}};
endmodule

module Shift_Right_Algorithm_8bit_complete (
  input  [7:0] in_1,
  input  [2:0] in_2,
  output [7:0] out_3
);

  wire [7:0] shift_right_algorithm_8bit_1_output_sra_0, shift_right_algorithm_8bit_1_output_sra_1,
       shift_right_algorithm_8bit_1_output_sra_2, shift_right_algorithm_8bit_1_output_sra_3,
       shift_right_algorithm_8bit_1_output_sra_4, shift_right_algorithm_8bit_1_output_sra_5,
       shift_right_algorithm_8bit_1_output_sra_6, shift_right_algorithm_8bit_1_output_sra_7;

  Shift_Right_Algorithm_8bit shift_right_algorithm_8bit_1 (
    .Data_input(in_1), .Output_sra_7(shift_right_algorithm_8bit_1_output_sra_7),
    .Output_sra_6(shift_right_algorithm_8bit_1_output_sra_6),
    .Output_sra_5(shift_right_algorithm_8bit_1_output_sra_5),
    .Output_sra_4(shift_right_algorithm_8bit_1_output_sra_4),
    .Output_sra_3(shift_right_algorithm_8bit_1_output_sra_3),
    .Output_sra_2(shift_right_algorithm_8bit_1_output_sra_2),
    .Output_sra_1(shift_right_algorithm_8bit_1_output_sra_1),
    .Output_sra_0(shift_right_algorithm_8bit_1_output_sra_0));
  Multiplexer #(.select(3), .width(8)) multiplexer_1 (
    .in0(shift_right_algorithm_8bit_1_output_sra_0), .in1(shift_right_algorithm_8bit_1_output_sra_1),
    .in2(shift_right_algorithm_8bit_1_output_sra_2), .in3(shift_right_algorithm_8bit_1_output_sra_3),
    .in4(shift_right_algorithm_8bit_1_output_sra_4), .in5(shift_right_algorithm_8bit_1_output_sra_5),
    .in6(shift_right_algorithm_8bit_1_output_sra_6), .in7(shift_right_algorithm_8bit_1_output_sra_7),
    .out(out_3), .sel(in_2));
endmodule

module mux_4_in (
  input  in_1,
  input  in_2,
  input  in_3,
  input  in_4,
  input  [1:0] in_5,
  output out_6
);

  wire decoder_1_out0, decoder_1_out1, decoder_1_out2, decoder_1_out3;

  Decoder #(.enable("false"), .select(2)) decoder_1 (
    .out0(decoder_1_out0), .out1(decoder_1_out1), .out2(decoder_1_out2), .out3(decoder_1_out3), .sel(in_5));
  assign out_6 = decoder_1_out2 ? in_2 : 1'bz;  // Controlled_Buffer controlled_buffer_1
  assign out_6 = decoder_1_out1 ? in_3 : 1'bz;  // Controlled_Buffer controlled_buffer_2
  assign out_6 = decoder_1_out0 ? in_4 : 1'bz;  // Controlled_Buffer controlled_buffer_3
  assign out_6 = decoder_1_out3 ? in_1 : 1'bz;  // Controlled_Buffer controlled_buffer_4
endmodule
