// Logisim project my_memory.circ as structural Verilog
module Decoder_2_4 (
  input  Enable,
  input  A0,
  input  A1,
  output Y0,
  output Y1,
  output Y2,
  output Y3
);

  wire not_1_out, not_2_out, not_3_out, not_4_out;

  not not_1 (not_1_out, A1);
  not not_2 (not_2_out, A0);
  not not_3 (not_3_out, A1);
  not not_4 (not_4_out, A0);
  and and_1 (Y0, not_1_out, Enable, not_2_out);
  and and_2 (Y1, not_3_out, Enable, A0);
  and and_3 (Y2, A1, Enable, not_4_out);
  and and_4 (Y3, A1, Enable, A0);
endmodule

module SR_latch (
  input  S_D,
  input  S,
  input  R,
  input  R_D,
  output Q,
  output QN
);

  wire not_1_out, not_2_out, not_3_out, not_4_out;

  not not_1 (not_1_out, S_D);
  not not_2 (not_2_out, S);
  not not_3 (not_3_out, R);
  not not_4 (not_4_out, R_D);
  nand nand_1 (Q, not_2_out, not_1_out, QN);
  nand nand_2 (QN, Q, not_4_out, not_3_out);
endmodule

module SR_electrical_level_flip_flop (
  input  S_D,
  input  S,
  input  Clock,
  input  R,
  input  R_D,
  output Q,
  output QN
);

  wire and_1_out, and_2_out;

  and and_1 (and_1_out, S, Clock);
  and and_2 (and_2_out, Clock, R);
  SR_latch sr_latch_1 (.S_D(S_D), .S(and_1_out), .R(and_2_out), .R_D(R_D), .Q(Q), .QN(QN));
endmodule

module SR_impulse_flip_flop (
  input  S_D,
  input  S,
  input  R,
  input  Clock,
  input  R_D,
  output Q,
  output QN
);

  wire not_1_out, sr_electrical_level_flip_flop_1_q, sr_electrical_level_flip_flop_1_qn;

  not not_1 (not_1_out, Clock);
  SR_electrical_level_flip_flop sr_electrical_level_flip_flop_1 (
    .S_D(S_D), .S(S), .Clock(Clock), .R(R), .R_D(R_D), .Q(sr_electrical_level_flip_flop_1_q),
    .QN(sr_electrical_level_flip_flop_1_qn));
  SR_electrical_level_flip_flop sr_electrical_level_flip_flop_2 (
    .S_D(S_D), .S(sr_electrical_level_flip_flop_1_q), .Clock(not_1_out),
    .R(sr_electrical_level_flip_flop_1_qn), .R_D(R_D), .Q(Q), .QN(QN));
endmodule

module JK_latch (
  input  S,
  input  J,
  input  K,
  input  R,
  output Q,
  output QN
);

  wire and_1_out, and_2_out;

  and and_1 (and_1_out, QN, J);
  and and_2 (and_2_out, K, Q);
  SR_latch sr_latch_1 (.S_D(S), .S(and_1_out), .R(and_2_out), .R_D(R), .Q(Q), .QN(QN));
endmodule

module JK_electrical_level_flip_flop (
  input  S,
  input  J,
  input  Clock,
  input  K,
  input  R,
  output Q,
  output QN
);

  wire and_1_out, and_2_out;

  and and_1 (and_1_out, J, Clock);
  and and_2 (and_2_out, Clock, K);
  JK_latch jk_latch_1 (.S(S), .J(and_1_out), .K(and_2_out), .R(R), .Q(Q), .QN(QN));
endmodule

module JK_impulse_flip_flop (
  input  in_1,
  input  in_2,
  input  in_3,
  input  in_4,
  input  in_5,
  output Q,
  output QN
);

  wire jk_electrical_level_flip_flop_1_q, jk_electrical_level_flip_flop_1_qn, not_1_out;

  not not_1 (not_1_out, in_4);
  JK_electrical_level_flip_flop jk_electrical_level_flip_flop_1 (
    .S(in_1), .J(in_2), .Clock(in_4), .K(in_3), .R(in_5), .Q(jk_electrical_level_flip_flop_1_q),
    .QN(jk_electrical_level_flip_flop_1_qn));
  JK_electrical_level_flip_flop jk_electrical_level_flip_flop_2 (
    .S(in_1), .J(jk_electrical_level_flip_flop_1_q), .Clock(not_1_out),
    .K(jk_electrical_level_flip_flop_1_qn), .R(in_5), .Q(Q), .QN(QN));
endmodule

module D_edge_flip_flop (
  input  S,
  input  D,
  input  Clock,
  input  R,
  output Q,
  output QN
);

  wire not_1_out, not_2_out, sr_electrical_level_flip_flop_1_q, sr_electrical_level_flip_flop_1_qn;

  not not_1 (not_1_out, D);
  not not_2 (not_2_out, Clock);
  SR_electrical_level_flip_flop sr_electrical_level_flip_flop_1 (
    .S_D(S), .S(D), .Clock(not_2_out), .R(not_1_out), .R_D(R), .Q(sr_electrical_level_flip_flop_1_q),
    .QN(sr_electrical_level_flip_flop_1_qn));
  SR_electrical_level_flip_flop sr_electrical_level_flip_flop_2 (
    .S_D(S), .S(sr_electrical_level_flip_flop_1_q), .Clock(Clock), .R(sr_electrical_level_flip_flop_1_qn),
    .R_D(R), .Q(Q), .QN(QN));
endmodule

module JK_edge_flip_flop (
  input  S,
  input  J,
  input  K,
  input  Clock,
  input  R,
  output Q,
  output QN
);

  wire and_1_out, and_2_out, not_1_out, or_1_out;

  and and_1 (and_1_out, J, QN);
  not not_1 (not_1_out, K);
  and and_2 (and_2_out, not_1_out, Q);
  or or_1 (or_1_out, and_1_out, and_2_out);
  D_edge_flip_flop d_edge_flip_flop_1 (.S(S), .D(or_1_out), .Clock(Clock), .R(R), .Q(Q), .QN(QN));
endmodule

module memery_1x1_1bit (
  input  S,
  input  Output_enable,
  input  Write_enable,
  input  Data_input,
  input  Clock,
  input  R,
  output Data_output
);

  wire and_1_out, and_2_out, j_k_ff_1_q, not_1_out;

  not not_1 (not_1_out, Data_input);
  and and_1 (and_1_out, Write_enable, Data_input);
  and and_2 (and_2_out, Write_enable, not_1_out);
  J_K_Flip_Flop j_k_ff_1 (
    .J(and_1_out), .K(and_2_out), .clk(Clock), .Q(j_k_ff_1_q), .preset(S), .reset(R));  // open: Qn
  assign Data_output = Output_enable ? j_k_ff_1_q : 1'bz;  // Controlled_Buffer controlled_buffer_1
endmodule

module memery_1x1_1bit_complete (
  input  Enable,
  input  S,
  input  Output_enable,
  input  Write_enable,
  input  Data_input,
  input  Clock,
  input  R,
  input  Row_addr,
  input  Col_addr,
  output out_10
);

  wire and_1_out, and_2_out, and_3_out, and_4_out, and_5_out, and_6_out, and_7_out;

  and and_1 (and_1_out, Row_addr, Col_addr);
  and and_2 (and_2_out, Enable, S);
  and and_3 (and_3_out, Enable, and_1_out, Output_enable);
  and and_4 (and_4_out, Enable, and_1_out, Write_enable);
  and and_5 (and_5_out, Enable, and_1_out, Data_input);
  and and_6 (and_6_out, Enable, and_1_out, Clock);
  and and_7 (and_7_out, Enable, R);
  memery_1x1_1bit memery_1x1_1bit_1 (
    .S(and_2_out), .Output_enable(and_3_out), .Write_enable(and_4_out), .Data_input(and_5_out),
    .Clock(and_6_out), .R(and_7_out), .Data_output(out_10));
endmodule

module memery_2x2_1bit (
  input  Enable,
  input  S,
  input  Output_enable,
  input  Write_enable,
  input  Data_input,
  input  Clock,
  input  R,
  input  Row_0,
  input  Row_1,
  input  Col_0,
  input  Col_1,
  output out_12
);

  memery_1x1_1bit_complete memery_1x1_1bit_complete_1 (
    .Enable(Enable), .S(S), .Output_enable(Output_enable), .Write_enable(Write_enable),
    .Data_input(Data_input), .Clock(Clock), .R(R), .Row_addr(Row_0), .Col_addr(Col_0), .out_10(out_12));
  memery_1x1_1bit_complete memery_1x1_1bit_complete_2 (
    .Enable(Enable), .S(S), .Output_enable(Output_enable), .Write_enable(Write_enable),
    .Data_input(Data_input), .Clock(Clock), .R(R), .Row_addr(Row_1), .Col_addr(Col_0), .out_10(out_12));
  memery_1x1_1bit_complete memery_1x1_1bit_complete_3 (
    .Enable(Enable), .S(S), .Output_enable(Output_enable), .Write_enable(Write_enable),
    .Data_input(Data_input), .Clock(Clock), .R(R), .Row_addr(Row_0), .Col_addr(Col_1), .out_10(out_12));
  memery_1x1_1bit_complete memery_1x1_1bit_complete_4 (
    .Enable(Enable), .S(S), .Output_enable(Output_enable), .Write_enable(Write_enable),
    .Data_input(Data_input), .Clock(Clock), .R(R), .Row_addr(Row_1), .Col_addr(Col_1), .out_10(out_12));
endmodule

module memery_2x1_complete (
  input  Enable,
  input  S,
  input  Output_enable,
  input  Write_enable,
  input  Data_input_1,
  input  Clock,
  input  R,
  input  [1:0] Address_2,
  output Data_ouput_1
);

  wire decoder_1_out0, decoder_1_out1, decoder_2_out0, decoder_2_out1;

  Decoder decoder_1 (.out0(decoder_1_out0), .out1(decoder_1_out1), .sel(Address_2[1]), .en(Enable));
  Decoder decoder_2 (.out0(decoder_2_out0), .out1(decoder_2_out1), .sel(Address_2[0]), .en(Enable));
  memery_2x2_1bit memery_2x2_1bit_1 (
    .Enable(Enable), .S(S), .Output_enable(Output_enable), .Write_enable(Write_enable),
    .Data_input(Data_input_1), .Clock(Clock), .R(R), .Row_0(decoder_2_out0), .Row_1(decoder_2_out1),
    .Col_0(decoder_1_out0), .Col_1(decoder_1_out1), .out_12(Data_ouput_1));
endmodule

module memory_2x4 (
  input  Enbale,
  input  S,
  input  Output_enable,
  input  Write_enable,
  input  [3:0] Data_input_4,
  input  Clock,
  input  R,
  input  [1:0] Address_2,
  output [3:0] Data_output_4
);

  memery_2x1_complete memery_2x1_complete_1 (
    .Enable(Enbale), .S(S), .Output_enable(Output_enable), .Write_enable(Write_enable),
    .Data_input_1(Data_input_4[0]), .Clock(Clock), .R(R), .Address_2(Address_2),
    .Data_ouput_1(Data_output_4[0]));
  memery_2x1_complete memery_2x1_complete_2 (
    .Enable(Enbale), .S(S), .Output_enable(Output_enable), .Write_enable(Write_enable),
    .Data_input_1(Data_input_4[1]), .Clock(Clock), .R(R), .Address_2(Address_2),
    .Data_ouput_1(Data_output_4[1]));
  memery_2x1_complete memery_2x1_complete_3 (
    .Enable(Enbale), .S(S), .Output_enable(Output_enable), .Write_enable(Write_enable),
    .Data_input_1(Data_input_4[2]), .Clock(Clock), .R(R), .Address_2(Address_2),
    .Data_ouput_1(Data_output_4[2]));
  memery_2x1_complete memery_2x1_complete_4 (
    .Enable(Enbale), .S(S), .Output_enable(Output_enable), .Write_enable(Write_enable),
    .Data_input_1(Data_input_4[3]), .Clock(Clock), .R(R), .Address_2(Address_2),
    .Data_ouput_1(Data_output_4[3]));
endmodule

module memory_2x8 (
  input  Enable,
  input  S,
  input  Output_enable,
  input  Write_enable,
  input  [7:0] Data_input_8,
  input  Clock,
  input  R,
  input  [1:0] Address_2,
  output [7:0] out_9
);

  memory_2x4 memory_2x4_1 (
    .Enbale(Enable), .S(S), .Output_enable(Output_enable), .Write_enable(Write_enable),
    .Data_input_4(Data_input_8[3:0]), .Clock(Clock), .R(R), .Address_2(Address_2), .Data_output_4(out_9[3:0]));
  memory_2x4 memory_2x4_2 (
    .Enbale(Enable), .S(S), .Output_enable(Output_enable), .Write_enable(Write_enable),
    .Data_input_4(Data_input_8[7:4]), .Clock(Clock), .R(R), .Address_2(Address_2), .Data_output_4(out_9[7:4]));
endmodule

module memory_4_8 (
  input  S,
  input  Output_enable,
  input  Write_enable,
  input  [7:0] Data_input_8,
  input  Clock,
  input  R,
  input  [3:0] Address_4,
  output [7:0] out_8
);

  wire decoder_1_out0, decoder_1_out1, decoder_1_out2, decoder_1_out3;

  Decoder #(.enable("false"), .select(2)) decoder_1 (
    .out0(decoder_1_out0), .out1(decoder_1_out1), .out2(decoder_1_out2), .out3(decoder_1_out3),
    .sel(Address_4[3:2]));
  memory_2x8 memory_2x8_1 (
    .Enable(decoder_1_out0), .S(S), .Output_enable(Output_enable), .Write_enable(Write_enable),
    .Data_input_8(Data_input_8), .Clock(Clock), .R(R), .Address_2(Address_4[1:0]), .out_9(out_8));
  memory_2x8 memory_2x8_2 (
    .Enable(decoder_1_out1), .S(S), .Output_enable(Output_enable), .Write_enable(Write_enable),
    .Data_input_8(Data_input_8), .Clock(Clock), .R(R), .Address_2(Address_4[1:0]), .out_9(out_8));
  memory_2x8 memory_2x8_3 (
    .Enable(decoder_1_out2), .S(S), .Output_enable(Output_enable), .Write_enable(Write_enable),
    .Data_input_8(Data_input_8), .Clock(Clock), .R(R), .Address_2(Address_4[1:0]), .out_9(out_8));
  memory_2x8 memory_2x8_4 (
    .Enable(decoder_1_out3), .S(S), .Output_enable(Output_enable), .Write_enable(Write_enable),
    .Data_input_8(Data_input_8), .Clock(Clock), .R(R), .Address_2(Address_4[1:0]), .out_9(out_8));
endmodule

module memory_4x8_complete (
  input  Enble,
  input  S,
  input  Output_enable,
  input  Write_enable,
  input  [7:0] Data_input_8,
  input  Clock,
  input  R,
  input  [3:0] Address_4,
  output [7:0] out_9
);

  wire and_1_out, and_2_out, and_3_out, and_4_out, and_5_out;

  and and_1 (and_1_out, Enble, S);
  and and_2 (and_2_out, Enble, Output_enable);
  buf and_3 (and_3_out, Write_enable);  // AND_Gate
  and and_4 (and_4_out, Enble, Clock);
  and and_5 (and_5_out, Enble, R);
  memory_4_8 memory_4_8_1 (
    .S(and_1_out), .Output_enable(and_2_out), .Write_enable(and_3_out), .Data_input_8(Data_input_8),
    .Clock(and_4_out), .R(and_5_out), .Address_4(Address_4), .out_8(out_9));
endmodule
